# Fritzing sketch Circuit Lampe Jedi (saved by Fritzing 0.9.3b)
circuit board: 6cm x 6cm
breadboards: 1

parts:
  Nano = Arduino Nano (Rev3.0)
  JACK2 = 2.1mm DC Barrel Jack
  C1 = Electrolytic Capacitor [capacitance=0.47mF voltage=16V package="200 mil [THT, electrolytic]"]
  Q2 = NPN-Transistor [package="TO92 [THT]"]
  R2 = Resistor [tolerance=±5% resistance=10k package=THT]
  R3 = Resistor [tolerance=±5% resistance=330 package=THT]
  J1 = female pin header, 2 pins [form="♀ (female)"]
  J2 = female pin header, 2 pins [form="♀ (female)"]
  R1 = Resistor [tolerance=±5% resistance=10k package=THT]
  R4 = Resistor [tolerance=±5% resistance=100k package=THT]
  J3 = female pin header, 2 pins [form="♀ (female)"]
  P1 = S1133 Si Photodiode [package="8mm Ceramic [THT]"]
  C2 = Electrolytic Capacitor [capacitance=0.47mF voltage=16V package="200 mil [THT, electrolytic]"]
  Q1 = NPN-Transistor [package="TO92 [THT]"]
  J4 = female pin header, 3 pins [form="♀ (female)"]

nets:
  N1: Nano.D0/RX, R1.Pin_0
  N2: Nano.GND, JACK2.sleeve, C1.-, Q2.E, R4.Pin_1, C2.-, Q1.E, J4.pin1
  N3: Nano.D2, R2.Pin_0
  N4: Nano.D3, J4.pin2
  N5: Nano.VIN, JACK2.center, C1.+, J1.pin2, J2.pin2
  N6: Nano.5V, J3.pin1, P1.cathode, C2.+, J4.pin3
  N7: Nano.A0, R4.Pin_0, J3.pin2, P1.anode
  N8: Q2.B, R2.Pin_1
  N9: Q2.C, J2.pin1
  N10: R3.Pin_0, Q1.C
  N11: R3.Pin_1, J1.pin1
  N12: R1.Pin_1, Q1.B

notes:
  Lum
  Rx
  Tx
  M
  12v

custom parts:
  2.1mm DC Barrel Jack: 2.1mm DC Barrel Jack with Thru-Hole Connectors (breadboardable)
